# Fritzing sketch bikesharelayout (saved by Fritzing 0.9.3b)
breadboards: 1

parts:
  Part1 = Arduino Uno (Rev3)
  R1 = Resistor [tolerance=±5% resistance=220 package=THT]
  LED1 = RGB LED (com. cathode, rbg) [package="5 mm [THT]"]
  LED2 = RGB LED (com. cathode, rbg) [package="5 mm [THT]"]
  C3 = Capacitor [package=cap-pth-small]
  C4 = Capacitor [package=cap-pth-small]
  LED3 = RGB LED (com. cathode, rbg) [package="5 mm [THT]"]
  C5 = Capacitor [package=cap-pth-small]
  C1 = Electrolytic Capacitor [capacitance=1µF package="100 mil [THT, electrolytic]"]
  Power_plug1 = Power plug  # not connected
  Raspberry_Pi_1 = Raspberry Pi 3 [part_number=RPI-3-V1.2]  # not connected

nets:
  N1: Part1.D6_PWM, R1.Pin_0
  N2: Part1.GND, LED1.blue_anode, LED2.blue_anode, C3.2, C4.2, LED3.blue_anode, C5.2, C1.+
  N3: R1.Pin_1, LED1.red_anode
  N4: LED1.common_cathode, LED2.common_cathode, C3.1, C4.1, LED3.common_cathode, C5.1, C1.-
  N5: LED1.green_anode, LED2.red_anode
  N6: LED2.green_anode, LED3.red_anode
