# Fritzing sketch neopixeltestlayout (saved by Fritzing 0.9.2b)
breadboards: 1

parts:
  Part1 = Arduino Uno (Rev3)
  C1 = Ceramic Capacitor [capacitance=1mF part_number="actually 220 MFD 25V" voltage=20V package="0805 [SMD, multilayer]"]
  R1 = Resistor [tolerance=±5% resistance=470 package="2512 [SMD]"]
  LED2 = RGB LED (com. cathode, rgb) [package="5 mm [THT]"]
  LED1 = RGB LED (com. cathode, rbg) [part_number="neopixel cut to the right" package="5 mm [THT]"]

nets:
  N1: Part1.D6_PWM, R1.Pin_0
  N2: Part1.5V, C1.1, LED2.common_cathode, LED1.common_cathode
  N3: Part1.GND, C1.0, LED2.green_anode, LED1.blue_anode
  N4: R1.Pin_1, LED1.red_anode
  N5: LED2.red_anode, LED1.green_anode
